# Fritzing sketch SchematischeTekening (saved by Fritzing 0.9.2b)
breadboards: 1

parts:
  Onderdeel1 = Arduino Uno (Rev3)
  Onderdeel2 = RFID-RC522-v2
  KEYPAD1 = Membrane Matrix Keypad

nets:
  N1: Onderdeel1.A0, Onderdeel2.RST
  N2: Onderdeel1.D8, KEYPAD1.2
  N3: Onderdeel1.D9_PWM, KEYPAD1.1
  N4: Onderdeel1.D10_PWM/SS, Onderdeel2.SDA
  N5: Onderdeel1.D11_PWM/MOSI, Onderdeel2.MOSI
  N6: Onderdeel1.D12/MISO, Onderdeel2.MISO
  N7: Onderdeel1.D13/SCK, Onderdeel2.SCK
  N8: Onderdeel1.D3_PWM, KEYPAD1.7
  N9: Onderdeel1.D4, KEYPAD1.6
  N10: Onderdeel1.D5_PWM, KEYPAD1.5
  N11: Onderdeel1.D6_PWM, KEYPAD1.4
  N12: Onderdeel1.D7, KEYPAD1.3
  3V3: Onderdeel1.3V3, Onderdeel2.3.3V
  GND: Onderdeel1.GND, Onderdeel2.GND

custom parts:
  RFID-RC522-v2: A simple China made RFID-RC522 Reader; do check the pin labels, as this is a MFRC522 based clone.
  Membrane Matrix Keypad: Membrane Matrix 3x4 Keypad
